// Logisim project control-logic.circ as structural Verilog: 1 circuit, main circuit control_logic
module control_logic (
  input  [31:0] Instruction,
  input  BrEq,
  input  BrLt,
  output PCSel,
  output RegWEn,
  output [2:0] ImmSel,
  output BrUn,
  output ASel,
  output BSel,
  output [3:0] ALUSel,
  output MemWEn,
  output [1:0] WBSel
);

  wire branch_equal, branch_greater_or_equal, branch_less, branch_not_equal, comparator_6_eq,
       comparator_7_eq, comparator_8_eq, comparator_9_eq, comparator_10_eq, comparator_11_eq,
       comparator_12_eq, comparator_13_eq, comparator_14_eq, comparator_15_eq, comparator_16_eq,
       comparator_17_eq, comparator_18_eq, comparator_19_eq, comparator_24_eq, comparator_25_eq,
       comparator_26_eq, comparator_27_eq, comparator_28_eq, comparator_29_eq, comparator_30_eq,
       comparator_31_eq, comparator_35_eq, comparator_36_eq, comparator_37_eq, comparator_38_eq,
       comparator_39_eq, comparator_40_eq, comparator_41_eq, comparator_42_eq, comparator_43_eq,
       comparator_44_eq, comparator_45_eq, comparator_46_eq, is_add, is_add0, is_addi, is_and, is_and0,
       is_andi, is_auipc, is_beq, is_bge, is_bgeu, is_blt, is_bltu, is_bne, is_btype, is_itype, is_jal,
       is_jalr, is_lb, is_lh, is_lui, is_lw, is_mul, is_mul0, is_mulh, is_mulh0, is_mulhu, is_mulhu0, is_or,
       is_or0, is_ori, is_rtype, is_sb, is_sh, is_sll, is_sll0, is_slli, is_slt, is_slt0, is_slti, is_sra,
       is_sra0, is_srai, is_srl, is_srl0, is_srli, is_stype, is_sub, is_sub0, is_sw, is_xor, is_xor0,
       is_xori, or_1_out, or_2_out;
  wire [5:0] ROMInput;
  wire [15:14] rom_1_data;

  Comparator #(.width(3)) comparator_1 (.a(Instruction[14:12]), .b(3'b000), .eq(is_add));  // open: gt, lt
  Comparator #(.width(3)) comparator_2 (.a(Instruction[14:12]), .b(3'b111), .eq(is_and));  // open: gt, lt
  Comparator #(.width(3)) comparator_3 (.a(Instruction[14:12]), .b(3'b110), .eq(is_or));  // open: gt, lt
  Comparator #(.width(3)) comparator_4 (.a(Instruction[14:12]), .b(3'b100), .eq(is_xor));  // open: gt, lt
  Comparator #(.width(3)) comparator_5 (.a(Instruction[14:12]), .b(3'b010), .eq(is_slt));  // open: gt, lt
  Comparator #(.width(3)) comparator_6 (.a(Instruction[14:12]), .b(3'b001), .eq(comparator_6_eq));  // open: gt, lt
  Comparator #(.width(7)) comparator_7 (.a(Instruction[31:25]), .b({7{1'b0}}), .eq(comparator_7_eq));  // open: gt, lt
  Comparator #(.width(3)) comparator_8 (.a(Instruction[14:12]), .b(3'b101), .eq(comparator_8_eq));  // open: gt, lt
  Comparator #(.width(7)) comparator_9 (.a(Instruction[31:25]), .b({7{1'b0}}), .eq(comparator_9_eq));  // open: gt, lt
  Comparator #(.width(3)) comparator_10 (.a(Instruction[14:12]), .b(3'b101), .eq(comparator_10_eq));  // open: gt, lt
  Comparator #(.width(7)) comparator_11 (
    .a(Instruction[31:25]), .b(7'b0100000), .eq(comparator_11_eq));  // open: gt, lt
  Comparator #(.width(3)) comparator_12 (.a(Instruction[14:12]), .b(3'b000), .eq(comparator_12_eq));  // open: gt, lt
  Comparator #(.width(7)) comparator_13 (
    .a(Instruction[31:25]), .b(7'b0000001), .eq(comparator_13_eq));  // open: gt, lt
  Comparator #(.width(3)) comparator_14 (.a(Instruction[14:12]), .b(3'b001), .eq(comparator_14_eq));  // open: gt, lt
  Comparator #(.width(7)) comparator_15 (
    .a(Instruction[31:25]), .b(7'b0000001), .eq(comparator_15_eq));  // open: gt, lt
  Comparator #(.width(3)) comparator_16 (.a(Instruction[14:12]), .b(3'b011), .eq(comparator_16_eq));  // open: gt, lt
  Comparator #(.width(7)) comparator_17 (
    .a(Instruction[31:25]), .b(7'b0000001), .eq(comparator_17_eq));  // open: gt, lt
  Comparator #(.width(3)) comparator_18 (.a(Instruction[14:12]), .b(3'b000), .eq(comparator_18_eq));  // open: gt, lt
  Comparator #(.width(7)) comparator_19 (
    .a(Instruction[31:25]), .b(7'b0100000), .eq(comparator_19_eq));  // open: gt, lt
  // Probe on is_add
  // Probe on is_and
  // Probe on is_or
  // Probe on is_xor
  // Probe on is_slt
  // Probe on is_sll
  and and_1 (is_sll, comparator_6_eq, comparator_7_eq);
  // Probe on is_srl
  and and_2 (is_srl, comparator_8_eq, comparator_9_eq);
  // Probe on is_sra
  and and_3 (is_sra, comparator_10_eq, comparator_11_eq);
  // Probe on is_mul
  and and_4 (is_mul, comparator_12_eq, comparator_13_eq);
  // Probe on is_mulh
  and and_5 (is_mulh, comparator_14_eq, comparator_15_eq);
  // Probe on is_mulhu
  and and_6 (is_mulhu, comparator_16_eq, comparator_17_eq);
  // Probe on is_sub
  and and_7 (is_sub, comparator_18_eq, comparator_19_eq);
  ROM #(.addrWidth(6), .dataWidth(16)) rom_1 (
    .addr(ROMInput), .data({rom_1_data, WBSel, MemWEn, ALUSel, BSel, ASel, BrUn, ImmSel, RegWEn}));
  // Probe on is_addi
  and and_8 (is_addi, is_itype, is_add);
  // Probe on is_andi
  and and_9 (is_andi, is_itype, is_and);
  // Probe on is_ori
  and and_10 (is_ori, is_itype, is_or);
  // Probe on is_xori
  and and_11 (is_xori, is_itype, is_xor);
  // Probe on is_slli
  and and_12 (is_slli, is_itype, is_sll);
  // Probe on is_srli
  and and_13 (is_srli, is_itype, is_srl);
  // Probe on is_srai
  and and_14 (is_srai, is_itype, is_sra);
  // Probe on is_slti
  and and_15 (is_slti, is_itype, is_slt);
  // Probe on is_add0
  and and_16 (is_add0, is_rtype, is_add);
  // Probe on is_and0
  and and_17 (is_and0, is_rtype, is_and);
  // Probe on is_or0
  and and_18 (is_or0, is_rtype, is_or);
  // Probe on is_xor0
  and and_19 (is_xor0, is_rtype, is_xor);
  // Probe on is_sll0
  and and_20 (is_sll0, is_rtype, is_sll);
  // Probe on is_srl0
  and and_21 (is_srl0, is_rtype, is_srl);
  // Probe on is_sra0
  and and_22 (is_sra0, is_rtype, is_sra);
  // Probe on is_slt0
  and and_23 (is_slt0, is_rtype, is_slt);
  // Probe on is_mul0
  and and_24 (is_mul0, is_rtype, is_mul);
  // Probe on is_mulh0
  and and_25 (is_mulh0, is_rtype, is_mulh);
  // Probe on is_mulhu0
  and and_26 (is_mulhu0, is_rtype, is_mulhu);
  // Probe on is_sub0
  and and_27 (is_sub0, is_rtype, is_sub);
  Comparator #(.width(7)) comparator_20 (.a(Instruction[6:0]), .b(7'b0010011), .eq(is_itype));  // open: gt, lt
  Comparator #(.width(7)) comparator_21 (.a(Instruction[6:0]), .b(7'b0110011), .eq(is_rtype));  // open: gt, lt
  Comparator #(.width(7)) comparator_22 (.a(Instruction[6:0]), .b(7'b1100011), .eq(is_btype));  // open: gt, lt
  Comparator #(.width(7)) comparator_23 (.a(Instruction[6:0]), .b(7'b0100011), .eq(is_stype));  // open: gt, lt
  Comparator #(.width(3)) comparator_24 (.a(Instruction[14:12]), .b(3'b000), .eq(comparator_24_eq));  // open: gt, lt
  Comparator #(.width(3)) comparator_25 (.a(Instruction[14:12]), .b(3'b101), .eq(comparator_25_eq));  // open: gt, lt
  Comparator #(.width(3)) comparator_26 (.a(Instruction[14:12]), .b(3'b111), .eq(comparator_26_eq));  // open: gt, lt
  Comparator #(.width(3)) comparator_27 (.a(Instruction[14:12]), .b(3'b100), .eq(comparator_27_eq));  // open: gt, lt
  Comparator #(.width(3)) comparator_28 (.a(Instruction[14:12]), .b(3'b110), .eq(comparator_28_eq));  // open: gt, lt
  Comparator #(.width(3)) comparator_29 (.a(Instruction[14:12]), .b(3'b001), .eq(comparator_29_eq));  // open: gt, lt
  // Probe on is_itype
  // Probe on is_rtype
  // Probe on is_btype
  // Probe on is_stype
  and and_28 (is_beq, comparator_24_eq, is_btype);
  and and_29 (is_bge, comparator_25_eq, is_btype);
  and and_30 (is_bgeu, comparator_26_eq, is_btype);
  and and_31 (is_blt, comparator_27_eq, is_btype);
  and and_32 (is_bltu, comparator_28_eq, is_btype);
  and and_33 (is_bne, comparator_29_eq, is_btype);
  // Probe on is_beq
  // Probe on is_bge
  // Probe on is_bgeu
  // Probe on is_blt
  // Probe on is_bltu
  // Probe on is_bne
  and and_34 (branch_equal, BrEq, is_beq);
  and and_35 (branch_not_equal, ~BrEq, is_bne);  // AND_Gate
  and and_36 (branch_less, BrLt, or_1_out);
  or or_1 (or_1_out, is_bltu, is_blt);
  and and_37 (branch_greater_or_equal, ~BrLt, or_2_out);  // AND_Gate
  or or_2 (or_2_out, is_bge, is_bgeu);
  Comparator #(.width(3)) comparator_30 (.a(Instruction[14:12]), .b(3'b000), .eq(comparator_30_eq));  // open: gt, lt
  Comparator #(.width(7)) comparator_31 (.a(Instruction[6:0]), .b(7'b1100111), .eq(comparator_31_eq));  // open: gt, lt
  Comparator #(.width(7)) comparator_32 (.a(Instruction[6:0]), .b(7'b0010111), .eq(is_auipc));  // open: gt, lt
  Comparator #(.width(7)) comparator_33 (.a(Instruction[6:0]), .b(7'b0110111), .eq(is_lui));  // open: gt, lt
  Comparator #(.width(7)) comparator_34 (.a(Instruction[6:0]), .b(7'b1101111), .eq(is_jal));  // open: gt, lt
  and and_38 (is_jalr, comparator_30_eq, comparator_31_eq);
  // Probe on is_auipc
  // Probe on is_lui
  Priority_Encoder #(.select_enc(6)) priority_encoder_1 (
    .in0(is_add0), .in1(is_mul0), .in2(is_sub0), .in3(is_sll0), .in4(is_mulh0), .in5(is_mulhu0),
    .in6(is_slt0), .in7(is_xor0), .in8(is_srl0), .in9(is_sra0), .in10(is_or0), .in11(is_and0), .in12(is_lb),
    .in13(is_lh), .in14(is_lw), .in15(is_addi), .in16(is_slli), .in17(is_slti), .in18(is_xori),
    .in19(is_srli), .in20(is_srai), .in21(is_ori), .in22(is_andi), .in23(is_sb), .in24(is_sh), .in25(is_sw),
    .in26(is_beq), .in27(is_bne), .in28(is_blt), .in29(is_bge), .in30(is_bltu), .in31(is_bgeu),
    .in32(is_auipc), .in33(is_lui), .in34(is_jal), .in35(is_jalr), .out(ROMInput));  // open: in36, in37, in38, in39, in40, in41, in42, in43, in44, in45, in46, in47, in48, in49, in50, in51, in52, in53, in54, in55, in56, in57, in58, in59, in60, in61, in62, in63, gs, en_out, en_in
  or or_3 (PCSel, is_jal, branch_equal, branch_not_equal, branch_less, branch_greater_or_equal, is_jalr);
  // Probe on is_jal
  // Probe on is_jalr
  // Probe on ROMInput
  Comparator #(.width(3)) comparator_35 (.a(Instruction[14:12]), .b(3'b000), .eq(comparator_35_eq));  // open: gt, lt
  Comparator #(.width(7)) comparator_36 (.a(Instruction[6:0]), .b(7'b0000011), .eq(comparator_36_eq));  // open: gt, lt
  Comparator #(.width(3)) comparator_37 (.a(Instruction[14:12]), .b(3'b001), .eq(comparator_37_eq));  // open: gt, lt
  Comparator #(.width(7)) comparator_38 (.a(Instruction[6:0]), .b(7'b0000011), .eq(comparator_38_eq));  // open: gt, lt
  Comparator #(.width(3)) comparator_39 (.a(Instruction[14:12]), .b(3'b010), .eq(comparator_39_eq));  // open: gt, lt
  Comparator #(.width(7)) comparator_40 (.a(Instruction[6:0]), .b(7'b0000011), .eq(comparator_40_eq));  // open: gt, lt
  Comparator #(.width(3)) comparator_41 (.a(Instruction[14:12]), .b(3'b000), .eq(comparator_41_eq));  // open: gt, lt
  Comparator #(.width(7)) comparator_42 (.a(Instruction[6:0]), .b(7'b0100011), .eq(comparator_42_eq));  // open: gt, lt
  Comparator #(.width(3)) comparator_43 (.a(Instruction[14:12]), .b(3'b001), .eq(comparator_43_eq));  // open: gt, lt
  Comparator #(.width(7)) comparator_44 (.a(Instruction[6:0]), .b(7'b0100011), .eq(comparator_44_eq));  // open: gt, lt
  Comparator #(.width(3)) comparator_45 (.a(Instruction[14:12]), .b(3'b010), .eq(comparator_45_eq));  // open: gt, lt
  Comparator #(.width(7)) comparator_46 (.a(Instruction[6:0]), .b(7'b0100011), .eq(comparator_46_eq));  // open: gt, lt
  and and_39 (is_lb, comparator_35_eq, comparator_36_eq);
  and and_40 (is_lh, comparator_37_eq, comparator_38_eq);
  and and_41 (is_lw, comparator_39_eq, comparator_40_eq);
  and and_42 (is_sb, comparator_41_eq, comparator_42_eq);
  and and_43 (is_sh, comparator_43_eq, comparator_44_eq);
  and and_44 (is_sw, comparator_45_eq, comparator_46_eq);
  // Probe on is_lb
  // Probe on is_lh
  // Probe on is_lw
  // Probe on is_sb
  // Probe on is_sh
  // Probe on is_sw

  // Other names for the same wires on the sheet: opcode[6:0] = Instruction[6:0]; funct3[2:0] = Instruction[14:12];
  //   funct7[6:0] = Instruction[31:25]

  // Notes on the sheet:
  //   INPUTS to your circuit
  //   contents of rom_1 (hex, n*v repeats v):
  //   1001 1401 1601 1081 1481 1581 1101 1201 1281 1681 1301 1381 41 41 41 1041 10c1 1141 1241 12c1 16c1
  //   1341 13c1 842 842 842 4*1064 1074 1074 1067 17c7 2069 2041
  //   ROM FOR CONTROL LOGIC
  //   DON'T CHANGE THE LOCATIONS OF THE INPUTS AND OUTPUTS!
  //   This is only if you choose to do the ROM option
  //   OUTPUT from your circuit
endmodule
