// Logisim project partial-load.circ as structural Verilog: 1 circuit, main circuit partial_load
module partial_load (
  input  [31:0] Instruction,
  input  [31:0] MemAddress,
  input  [31:0] DataFromMem,
  output [31:0] DataToReg
);

  wire comparator_1_eq, comparator_2_eq, comparator_3_eq, comparator_4_eq, comparator_5_eq, comparator_6_eq,
       is_lb, is_lh, is_lw;
  wire [1:0] value_selector;
  wire [7:0] multiplexer_2_out;
  wire [15:0] multiplexer_3_out;
  wire [31:0] lb_value, lh_value;

  Comparator #(.width(7)) comparator_1 (.a(Instruction[6:0]), .b(7'b0000011), .eq(comparator_1_eq));  // open: gt, lt
  Comparator #(.width(3)) comparator_2 (.a(Instruction[14:12]), .b(3'b000), .eq(comparator_2_eq));  // open: gt, lt
  Comparator #(.width(7)) comparator_3 (.a(Instruction[6:0]), .b(7'b0000011), .eq(comparator_3_eq));  // open: gt, lt
  Comparator #(.width(3)) comparator_4 (.a(Instruction[14:12]), .b(3'b001), .eq(comparator_4_eq));  // open: gt, lt
  Comparator #(.width(7)) comparator_5 (.a(Instruction[6:0]), .b(7'b0000011), .eq(comparator_5_eq));  // open: gt, lt
  Comparator #(.width(3)) comparator_6 (.a(Instruction[14:12]), .b(3'b010), .eq(comparator_6_eq));  // open: gt, lt
  and and_1 (is_lb, comparator_1_eq, comparator_2_eq);
  and and_2 (is_lh, comparator_3_eq, comparator_4_eq);
  and and_3 (is_lw, comparator_5_eq, comparator_6_eq);
  Multiplexer #(.select(2), .width(32)) multiplexer_1 (
    .in0(lb_value), .in1(lh_value), .in2(DataFromMem), .out(DataToReg), .sel(value_selector));  // open: in3
  assign lb_value = {{24{multiplexer_2_out[7]}}, multiplexer_2_out};  // Bit_Extender bit_extender_1
  Multiplexer #(.select(2), .width(8)) multiplexer_2 (
    .in0(DataFromMem[7:0]), .in1(DataFromMem[15:8]), .in2(DataFromMem[23:16]), .in3(DataFromMem[31:24]),
    .out(multiplexer_2_out), .sel(MemAddress[1:0]));
  assign lh_value = {{16{multiplexer_3_out[15]}}, multiplexer_3_out};  // Bit_Extender bit_extender_2
  Multiplexer #(.select(2), .width(16)) multiplexer_3 (
    .in0(DataFromMem[15:0]), .in1(DataFromMem[23:8]), .in2(DataFromMem[31:16]), .out(multiplexer_3_out),
    .sel(MemAddress[1:0]));  // open: in3
  Priority_Encoder #(.select_enc(2)) priority_encoder_1 (
    .in0(is_lb), .in1(is_lh), .in2(is_lw), .out(value_selector));  // open: in3, gs, en_out, en_in

  // Other names for the same wires on the sheet: byte1[7:0] = DataFromMem[15:8]; byte2[7:0] = DataFromMem[23:16];
  //   byte3[7:0] = DataFromMem[31:24]; byte0[7:0] = DataFromMem[7:0]; opcode[6:0] = Instruction[6:0];
  //   funct3[2:0] = Instruction[14:12]; funct7[6:0] = Instruction[31:25]; offset[1:0] = MemAddress[1:0]

  // Notes on the sheet:
  //   INPUTS to your circuit
  //   DON'T CHANGE THE LOCATIONS OF THE INPUTS AND OUTPUTS!
  //   OUTPUT from your circuit
endmodule
