// Logisim project partial-store.circ as structural Verilog: 1 circuit, main circuit partial_store
module partial_store (
  input  [31:0] Instruction,
  input  [31:0] MemAddress,
  input  [31:0] DataFromReg,
  input  MemWEn,
  output [3:0] MemWriteMask,
  output [31:0] DataToMem
);

  wire comparator_1_eq, comparator_2_eq, comparator_3_eq, comparator_4_eq, comparator_5_eq, comparator_6_eq,
       is_sb, is_sh, is_sw, NonStore;
  wire [1:0] value_selector;
  wire [3:0] sb_mask, sh_mask;
  wire [31:0] sb_value, sh_value;

  Comparator #(.width(7)) comparator_1 (.a(Instruction[6:0]), .b(7'b0100011), .eq(comparator_1_eq));  // open: gt, lt
  Comparator #(.width(3)) comparator_2 (.a(Instruction[14:12]), .b(3'b000), .eq(comparator_2_eq));  // open: gt, lt
  Comparator #(.width(7)) comparator_3 (.a(Instruction[6:0]), .b(7'b0100011), .eq(comparator_3_eq));  // open: gt, lt
  Comparator #(.width(3)) comparator_4 (.a(Instruction[14:12]), .b(3'b001), .eq(comparator_4_eq));  // open: gt, lt
  Comparator #(.width(7)) comparator_5 (.a(Instruction[6:0]), .b(7'b0100011), .eq(comparator_5_eq));  // open: gt, lt
  Comparator #(.width(3)) comparator_6 (.a(Instruction[14:12]), .b(3'b010), .eq(comparator_6_eq));  // open: gt, lt
  and and_1 (is_sb, comparator_1_eq, comparator_2_eq);
  and and_2 (is_sh, comparator_3_eq, comparator_4_eq);
  and and_3 (is_sw, comparator_5_eq, comparator_6_eq);
  not not_1 (NonStore, MemWEn);
  Multiplexer #(.select(2), .width(32)) multiplexer_1 (
    .in0(sb_value), .in1(sh_value), .in2(DataFromReg), .in3(DataFromReg), .out(DataToMem),
    .sel(value_selector));
  Multiplexer #(.select(2), .width(32)) multiplexer_2 (
    .in0({{24{1'b0}}, DataFromReg[7:0]}), .in1({{16{1'b0}}, DataFromReg[7:0], {8{1'b0}}}),
    .in2({{8{1'b0}}, DataFromReg[7:0], {16{1'b0}}}), .in3({DataFromReg[7:0], {24{1'b0}}}), .out(sb_value),
    .sel(MemAddress[1:0]));
  Multiplexer #(.select(2), .width(4)) multiplexer_3 (
    .in0(4'b0001), .in1(4'b0010), .in2(4'b0100), .in3(4'b1000), .out(sb_mask), .sel(MemAddress[1:0]));
  Priority_Encoder #(.select_enc(2)) priority_encoder_1 (
    .in0(is_sb), .in1(is_sh), .in2(is_sw), .in3(NonStore), .out(value_selector));  // open: gs, en_out, en_in
  Multiplexer #(.select(2), .width(32)) multiplexer_4 (
    .in0({{16{1'b0}}, DataFromReg[15:0]}), .in2({DataFromReg[15:0], {16{1'b0}}}), .out(sh_value),
    .sel(MemAddress[1:0]));  // open: in1, in3
  Multiplexer #(.select(2), .width(4)) multiplexer_5 (
    .in0(4'b0011), .in2(4'b1100), .out(sh_mask), .sel(MemAddress[1:0]));  // open: in1, in3
  Multiplexer #(.select(2), .width(4)) multiplexer_6 (
    .in0(sb_mask), .in1(sh_mask), .in2(4'b1111), .in3(4'b0000), .out(MemWriteMask), .sel(value_selector));

  // Other names for the same wires on the sheet: byte0[7:0] = DataFromReg[7:0]; half_word[15:0] = DataFromReg[15:0];
  //   byte1[7:0] = DataFromReg[15:8]; byte2[7:0] = DataFromReg[23:16]; byte3[7:0] = DataFromReg[31:24];
  //   opcode[6:0] = Instruction[6:0]; funct3[2:0] = Instruction[14:12]; funct7[6:0] = Instruction[31:25];
  //   offset[1:0] = MemAddress[1:0]

  // Notes on the sheet:
  //   INPUTS to your circuit
  //   DON'T CHANGE THE LOCATIONS OF THE INPUTS AND OUTPUTS!
  //   OUTPUT from your circuit
endmodule
