// Logisim project regfile.circ as structural Verilog: 1 circuit, main circuit regfile
module regfile (
  input  [4:0] ReadIndex1,
  input  [4:0] ReadIndex2,
  input  [4:0] WriteIndex,
  input  [31:0] WriteData,
  input  RegWEn,
  input  clk,
  output [31:0] ra,
  output [31:0] sp,
  output [31:0] t0,
  output [31:0] t1,
  output [31:0] t2,
  output [31:0] s0,
  output [31:0] s1,
  output [31:0] a0,
  output [31:0] ReadData1,
  output [31:0] ReadData2
);

  wire a0Write, a1Write, a2Write, a3Write, a4Write, a5Write, a6Write, a7Write, gpWrite, raWrite, s0Write,
       s1Write, s2Write, s3Write, s4Write, s5Write, s6Write, s7Write, s8Write, s9Write, s10Write, s11Write,
       spWrite, t0Write, t1Write, t2Write, t3Write, t4Write, t5Write, t6Write, tpWrite;
  wire [31:0] a1, a2, a3, a4, a5, a6, a7, gp, s2, s3, s4, s5, s6, s7, s8, s9, s10, s11, t3, t4, t5, t6, tp,
       zero;

  Register #(.width(32)) x0 (.D({32{1'b0}}), .en(1'b0), .clk(clk), .Q(zero));  // open: clr
  Register #(.width(32)) x1 (.D(WriteData), .en(raWrite), .clk(clk), .Q(ra));  // open: clr
  Register #(.width(32)) x2 (.D(WriteData), .en(spWrite), .clk(clk), .Q(sp));  // open: clr
  Register #(.width(32)) x3 (.D(WriteData), .en(gpWrite), .clk(clk), .Q(gp));  // open: clr
  Register #(.width(32)) x4 (.D(WriteData), .en(tpWrite), .clk(clk), .Q(tp));  // open: clr
  Register #(.width(32)) x5 (.D(WriteData), .en(t0Write), .clk(clk), .Q(t0));  // open: clr
  Register #(.width(32)) x6 (.D(WriteData), .en(t1Write), .clk(clk), .Q(t1));  // open: clr
  Register #(.width(32)) x7 (.D(WriteData), .en(t2Write), .clk(clk), .Q(t2));  // open: clr
  Register #(.width(32)) x8 (.D(WriteData), .en(s0Write), .clk(clk), .Q(s0));  // open: clr
  Register #(.width(32)) x9 (.D(WriteData), .en(s1Write), .clk(clk), .Q(s1));  // open: clr
  Register #(.width(32)) x10 (.D(WriteData), .en(a0Write), .clk(clk), .Q(a0));  // open: clr
  Register #(.width(32)) x11 (.D(WriteData), .en(a1Write), .clk(clk), .Q(a1));  // open: clr
  Register #(.width(32)) x12 (.D(WriteData), .en(a2Write), .clk(clk), .Q(a2));  // open: clr
  Register #(.width(32)) x13 (.D(WriteData), .en(a3Write), .clk(clk), .Q(a3));  // open: clr
  Register #(.width(32)) x14 (.D(WriteData), .en(a4Write), .clk(clk), .Q(a4));  // open: clr
  Register #(.width(32)) x15 (.D(WriteData), .en(a5Write), .clk(clk), .Q(a5));  // open: clr
  Register #(.width(32)) x16 (.D(WriteData), .en(a6Write), .clk(clk), .Q(a6));  // open: clr
  Register #(.width(32)) x17 (.D(WriteData), .en(a7Write), .clk(clk), .Q(a7));  // open: clr
  Register #(.width(32)) x18 (.D(WriteData), .en(s2Write), .clk(clk), .Q(s2));  // open: clr
  Register #(.width(32)) x19 (.D(WriteData), .en(s3Write), .clk(clk), .Q(s3));  // open: clr
  Register #(.width(32)) x20 (.D(WriteData), .en(s4Write), .clk(clk), .Q(s4));  // open: clr
  Register #(.width(32)) x21 (.D(WriteData), .en(s5Write), .clk(clk), .Q(s5));  // open: clr
  Register #(.width(32)) x22 (.D(WriteData), .en(s6Write), .clk(clk), .Q(s6));  // open: clr
  Register #(.width(32)) x23 (.D(WriteData), .en(s7Write), .clk(clk), .Q(s7));  // open: clr
  Register #(.width(32)) x24 (.D(WriteData), .en(s8Write), .clk(clk), .Q(s8));  // open: clr
  Register #(.width(32)) x25 (.D(WriteData), .en(s9Write), .clk(clk), .Q(s9));  // open: clr
  Register #(.width(32)) x26 (.D(WriteData), .en(s10Write), .clk(clk), .Q(s10));  // open: clr
  Register #(.width(32)) x27 (.D(WriteData), .en(s11Write), .clk(clk), .Q(s11));  // open: clr
  Register #(.width(32)) x28 (.D(WriteData), .en(t3Write), .clk(clk), .Q(t3));  // open: clr
  Register #(.width(32)) x29 (.D(WriteData), .en(t4Write), .clk(clk), .Q(t4));  // open: clr
  Register #(.width(32)) x30 (.D(WriteData), .en(t5Write), .clk(clk), .Q(t5));  // open: clr
  Register #(.width(32)) x31 (.D(WriteData), .en(t6Write), .clk(clk), .Q(t6));  // open: clr
  Decoder #(.select(5)) decoder_1 (
    .out1(raWrite), .out2(spWrite), .out3(gpWrite), .out4(tpWrite), .out5(t0Write), .out6(t1Write),
    .out7(t2Write), .out8(s0Write), .out9(s1Write), .out10(a0Write), .out11(a1Write), .out12(a2Write),
    .out13(a3Write), .out14(a4Write), .out15(a5Write), .out16(a6Write), .out17(a7Write), .out18(s2Write),
    .out19(s3Write), .out20(s4Write), .out21(s5Write), .out22(s6Write), .out23(s7Write), .out24(s8Write),
    .out25(s9Write), .out26(s10Write), .out27(s11Write), .out28(t3Write), .out29(t4Write), .out30(t5Write),
    .out31(t6Write), .sel(WriteIndex), .en(RegWEn));  // open: out0
  Multiplexer #(.select(5), .width(32)) multiplexer_1 (
    .in0(zero), .in1(ra), .in2(sp), .in3(gp), .in4(tp), .in5(t0), .in6(t1), .in7(t2), .in8(s0), .in9(s1),
    .in10(a0), .in11(a1), .in12(a2), .in13(a3), .in14(a4), .in15(a5), .in16(a6), .in17(a7), .in18(s2),
    .in19(s3), .in20(s4), .in21(s5), .in22(s6), .in23(s7), .in24(s8), .in25(s9), .in26(s10), .in27(s11),
    .in28(t3), .in29(t4), .in30(t5), .in31(t6), .out(ReadData1), .sel(ReadIndex1));
  Multiplexer #(.select(5), .width(32)) multiplexer_2 (
    .in0(zero), .in1(ra), .in2(sp), .in3(gp), .in4(tp), .in5(t0), .in6(t1), .in7(t2), .in8(s0), .in9(s1),
    .in10(a0), .in11(a1), .in12(a2), .in13(a3), .in14(a4), .in15(a5), .in16(a6), .in17(a7), .in18(s2),
    .in19(s3), .in20(s4), .in21(s5), .in22(s6), .in23(s7), .in24(s8), .in25(s9), .in26(s10), .in27(s11),
    .in28(t3), .in29(t4), .in30(t5), .in31(t6), .out(ReadData2), .sel(ReadIndex2));

  // Notes on the sheet:
  //   INPUTS to your circuit
  //   DON'T CHANGE THE LOCATIONS OF THE INPUTS AND OUTPUTS!
  //   These are DEBUG/TEST outputs from your circuit.
  //   OUTPUTS from your circuit
endmodule
